# Fritzing sketch pololu_arduino (saved by Fritzing 0.9.0b)
breadboards: 1

parts:
  M1 = Stepper Motor - Bipolar
  C1 = Electrolytic Capacitor [capacitance=0.1mF voltage=0.1kV package="100 mil [THT, electrolytic]"]
  Power_plug = Power plug
  Part1 = Arduino Mega 2560 (Rev3)
  DRV8824/8834 = DRV8824

nets:
  N1: M1.A, DRV8824/8834.11_-_A1
  N2: M1.C, DRV8824/8834.10_-_A2
  N3: M1.B, DRV8824/8834.12_-_B1
  N4: M1.D, DRV8824/8834.13_-_B2
  GND: C1.-, Power_plug.GND, Part1.GND, DRV8824/8834.8_-_GND_logic, DRV8824/8834.14_-_GND_motor
  N5: C1.+, Power_plug.VCC, DRV8824/8834.15_-_VMOT
  N6: Part1.5V, DRV8824/8834.9_-_/FAULT
  N7: Part1.D30, DRV8824/8834.7_-_DIR
  N8: Part1.D32, DRV8824/8834.6_-_STEP

custom parts:
  DRV8824: Pololu DRV8824 Stepper Motor Control Breakout The DRV8824 stepper motor driver carrier is a breakout board for TI’s DRV8824 microstepping bipolar stepper motor driver, a lower-current version of the DRV8825. The DRV8824 carrier can only deliver up to 0.75 A per coil without a heat sink (it is rated for up to 1.2 A per coil with sufficient additional cooling), but it has larger current-sense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
