# Fritzing sketch pump-shield (saved by Fritzing 0.9.0b)
circuit board: 3.11602cm x 5.33999cm
breadboards: 1

parts:
  ANALOG = female pin header, 8 pins [form="♀ (female)"]  # not connected
  2_5-10_8V = Power plug
  POLOLU = DRV8824
  100uF = Electrolytic Capacitor [capacitance=0.1mF voltage=0.1kV package="100 mil [THT, electrolytic]"]
  STEPPER = female pin header, 4 pins [form="♀ (female)"]
  M1 = male pin header, 5 pins [form="♂ (male)"]
  ENCODER = female pin header, 6 pins [form="♀ (female)"]  # not connected
  DIGITAL = female pin header, 6 pins [form="♀ (female)"]

nets:
  N1: 2_5-10_8V.GND, POLOLU.14_-_GND_motor, 100uF.-
  N2: 2_5-10_8V.VCC, POLOLU.15_-_VMOT, 100uF.+
  N3: POLOLU.1_-_M0, M1.pin4
  N4: POLOLU.2_-_M1, M1.pin5
  N5: POLOLU.6_-_STEP, M1.pin2
  N6: POLOLU.7_-_DIR, M1.pin3
  N7: POLOLU.8_-_GND_logic, DIGITAL.pin6
  N8: POLOLU.9_-_/FAULT, M1.pin1
  N9: POLOLU.10_-_A2, STEPPER.pin4
  N10: POLOLU.11_-_A1, STEPPER.pin3
  N11: POLOLU.12_-_B1, STEPPER.pin2
  N12: POLOLU.13_-_B2, STEPPER.pin1

notes:
  GND
  Pump Shield v0.1

custom parts:
  DRV8824: Pololu DRV8824 Stepper Motor Control Breakout The DRV8824 stepper motor driver carrier is a breakout board for TI’s DRV8824 microstepping bipolar stepper motor driver, a lower-current version of the DRV8825. The DRV8824 carrier can only deliver up to 0.75 A per coil without a heat sink (it is rated for up to 1.2 A per coil with sufficient additional cooling), but it has larger current-sense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
